# Fritzing sketch scheme (saved by Fritzing 0.9.3b)
breadboards: 1

parts:
  Part1 = Arduino Uno (Rev3)
  U1 = 555 Timer [package="DIP8 [THT]"]

nets:
  N1: Part1.D8, U1.Trigger
  N2: Part1.D10_PWM/SS, U1.Ground
  N3: Part1.D11_PWM/MOSI, U1.Reset
  N4: Part1.D13/SCK, U1.Output
  N5: Part1.GND, U1.Control_Voltage

notes:
  Car Battery 12V
  Car Ground
  Car LIN bus
  MCP2004
